# Fritzing sketch example-configuration (saved by Fritzing 0.9.3b)
breadboards: 1

parts:
  Raspberry_Pi1 = Raspberry Pi 2
  LED1 = LED - 3mm [color="Red (633nm)" package="3 mm [THT]"]
  S1 = SWITCH-MOMENTARY-2 [package=tactile-pth-12mm]

nets:
  N1: Raspberry_Pi1.GND, LED1.cathode, S1.1
  N2: Raspberry_Pi1.GPIO24, LED1.anode
